// Logisim project datapath_ula.circ as structural Verilog: 3 circuits, main circuit Datapath
module Datapath (
  input  [31:0] A,
  input  [31:0] B,
  input  [3:0] Controle_ALU,
  output Zero,
  output [31:0] Result,
  output Overflow
);

  // ALU alu_1: pin names not known; wires that end beside it: A, B, Controle_ALU, Zero, Result, Overflow, Overflow

  // Notes on the sheet:
  //   Controle ALU/ULA
  //   0000
  //   0001
  //   0010
  //   0110
  //   0111
  //   1100
  //   ALU
  //   and
  //   or
  //   add
  //   sub
  //   slt
  //   nor
  //   Função
endmodule

module Control (
  input  [8:0] teste,
  input  [5:0] op,
  output RegDst,
  output Branch,
  output LeMem,
  output MemparaReg,
  output [1:0] OpALU,
  output EscreveMem,
  output OrigALU,
  output EscreveReg
);


  assign Branch = teste[7];
  assign EscreveMem = teste[2];
  assign EscreveReg = teste[0];
  assign LeMem = teste[6];
  assign MemparaReg = teste[5];
  assign OpALU = {teste[3], teste[4]};
  assign OrigALU = teste[1];
  assign RegDst = teste[8];
endmodule

module ALUcontrol (
  input  [3:0] teste,
  input  [5:0] funct,
  input  [1:0] OpALU,
  output [3:0] Operation
);


  assign Operation = teste;
endmodule
